# Fritzing sketch AY-3-8912_AVR (saved by Fritzing 1.0.3b)
circuit board: 2.1484cm x 3.9cm
breadboards: 1

parts:
  IC1 = IC, DIP package, 28 pins [chip_label=IC]
  IC2 = IC, DIP package, 28 pins [chip_label=IC]
  R2 = Resistor [tolerance=±5% resistance=220 power=0.25W package="0805 [SMD]"]
  R3 = Resistor [tolerance=±5% resistance=220 power=0.25W package="0805 [SMD]"]
  27MHz = Resonator [frequency="16 Mhz" package=THT]
  XTAL1 = Crystal [frequency="16 Mhz" package=SMD]
  Pad1 = Pad [width=1.447542402831847 height=2.28342977344631 connect=center]
  R1 = Resistor [tolerance=±5% resistance=220 power=0.25W package="0805 [SMD]"]
  C1 = Ceramic Capacitor [capacitance=100nF voltage=35V package="0805 [SMD, multilayer]"]
  C3 = Ceramic Capacitor [capacitance="100 nF" voltage=35V package="0805 [SMD, multilayer]"]
  C4 = Ceramic Capacitor [capacitance="100 nF" voltage=35V package="0805 [SMD, multilayer]"]

nets:
  N1: IC1.pin1, R2.Pin_0, C1.1
  N2: IC1.pin2, IC2.pin17, R1.Pin_1
  N3: IC1.pin3, IC2.pin7
  N4: IC1.pin4, R1.Pin_0, C4.0
  N5: IC1.pin5, R3.Pin_0, C3.0
  N6: IC1.pin6, IC2.pin8, IC2.pin22, 27MHz.GND, Pad1.pad, C1.0, C3.1, C4.1
  N7: IC1.pin15, IC2.pin6
  N8: IC1.pin16, IC2.pin1
  N9: IC1.pin17, IC2.pin18
  N10: IC1.pin18, IC2.pin5
  N11: IC1.pin19, IC2.pin19
  N12: IC1.pin20, IC2.pin4
  N13: IC1.pin21, IC2.pin13
  N14: IC1.pin22, IC2.pin12
  N15: IC1.pin23, IC2.pin28
  N16: IC1.pin24, IC2.pin27
  N17: IC1.pin25, IC2.pin26
  N18: IC1.pin26, IC2.pin25
  N19: IC1.pin27, IC2.pin24
  N20: IC1.pin28, IC2.pin23
  N21: IC2.pin9, 27MHz.0, XTAL1.pin_0
  N22: IC2.pin10, 27MHz.pin_1, XTAL1.pin_1
  N23: IC2.pin15, R3.Pin_1
  N24: IC2.pin16, R2.Pin_1

notes:
  AVR-AY_LOWP VER. HEEMINYT
  HEEMINYT
