# Fritzing sketch MockingBoard (saved by Fritzing 1.0.3b)
circuit board: 19.05cm x 7.747cm
breadboards: 1

parts:
  J1 = Generic single row SMD female header - 25 pins [form="♀ (female)" package=THT]
  J2 = Generic single row SMD female header - 25 pins [form="♀ (female)" package=THT]
  KC89C72 = IC, DIP package, 40 pins [chip_label=IC]
  UM6522 = IC, DIP package, 40 pins [chip_label=IC]
  UM6522_2 = IC, DIP package, 40 pins [chip_label=IC]
  KC89C72_2 = IC, DIP package, 40 pins [chip_label=IC]
  Pad1 = Solder Mask Keepout FC Cartridge Connector  # not connected
  Pad2 = Solder Mask Keepout FC Cartridge Connector  # not connected
  TRS1 = Audio Jack (TRS) 3.5mm [package="4Ucon 08780 [THT]"]
  330R_ARRAY = Generic female header - 4 pins [form="♀ (female)" package=THT]
  330R_ARRAY_2 = Generic female header - 4 pins [form="♀ (female)" package=THT]
  10uF = Electrolytic Capacitor [capacitance=1µF voltage=35V package="100 mil [THT, electrolytic]"]
  10uF_2 = Electrolytic Capacitor [capacitance=1µF voltage=35V package="100 mil [THT, electrolytic]"]
  330 = Resistor [tolerance=±5% power=0.25W resistance=220 package=THT]
  330_2 = Resistor [tolerance=±5% power=0.25W resistance=220 package=THT]
  STEREO/MONO_SW = Toggle Switch [package=THT]
  74LS05 = 74HC04_HEX_INVERTER [package=dil14]
  IC1 = IC, DIP package, 14 pins [chip_label=IC]  # not connected
  1K_ARRAY = Generic female header - 4 pins [form="♀ (female)" package=THT]
  4K7_ARRAY = Generic female header - 4 pins [form="♀ (female)" package=THT]
  5pF = Ceramic Capacitor [capacitance=100nF voltage=35V package="100 mil [THT, multilayer]"]
  10uF_3 = Electrolytic Capacitor [capacitance=1µF voltage=35V package="100 mil [THT, electrolytic]"]
  J6 = molex pin header, 2 pins [form=molex]

nets:
  N1: J1.pin1, UM6522.pin23, UM6522_2.pin23
  N2: J1.pin2, UM6522.pin38, UM6522_2.pin38
  N3: J1.pin3, UM6522.pin37, UM6522_2.pin37
  N4: J1.pin4, UM6522.pin36, UM6522_2.pin36
  N5: J1.pin5, UM6522.pin35, UM6522_2.pin35
  N6: J1.pin9, UM6522_2.pin24, 74LS05.4A
  N7: J1.pin18, UM6522.pin22, UM6522_2.pin22
  N8: J1.pin25, KC89C72.pin25, KC89C72.pin28, KC89C72.pin40, UM6522.pin20, UM6522_2.pin20, KC89C72_2.pin25, KC89C72_2.pin28, KC89C72_2.pin40, 74LS05.VCC, 1K_ARRAY.pin1, 4K7_ARRAY.pin1, 10uF_3.+
  N9: J2.pin1, KC89C72.pin1, KC89C72.pin24, UM6522.pin1, UM6522_2.pin1, KC89C72_2.pin1, KC89C72_2.pin24, TRS1.Sleeve, 330.Pin_0, 330_2.Pin_0, 74LS05.GND, 10uF_3.-, J6.pin1
  N10: J2.pin4, UM6522_2.pin21
  N11: J2.pin5, UM6522.pin21
  N12: J2.pin6, UM6522.pin34, UM6522_2.pin34
  N13: J2.pin13, 74LS05.6A
  N14: J2.pin17, UM6522.pin26, UM6522_2.pin26
  N15: J2.pin18, UM6522.pin27, UM6522_2.pin27
  N16: J2.pin19, UM6522.pin28, UM6522_2.pin28
  N17: J2.pin20, UM6522.pin29, UM6522_2.pin29
  N18: J2.pin21, UM6522.pin30, UM6522_2.pin30
  N19: J2.pin22, UM6522.pin31, UM6522_2.pin31
  N20: J2.pin23, UM6522.pin32, UM6522_2.pin32
  N21: J2.pin24, UM6522.pin33, UM6522_2.pin33
  N22: KC89C72.pin3, 330R_ARRAY.pin4
  N23: KC89C72.pin4, 330R_ARRAY.pin3
  N24: KC89C72.pin23, UM6522.pin12
  N25: KC89C72.pin27, UM6522.pin11
  N26: KC89C72.pin29, UM6522.pin10
  N27: KC89C72.pin30, UM6522.pin9
  N28: KC89C72.pin31, UM6522.pin8
  N29: KC89C72.pin32, UM6522.pin7
  N30: KC89C72.pin33, UM6522.pin6
  N31: KC89C72.pin34, UM6522.pin5
  N32: KC89C72.pin35, UM6522.pin4
  N33: KC89C72.pin36, UM6522.pin3
  N34: KC89C72.pin37, UM6522.pin2
  N35: KC89C72.pin38, 330R_ARRAY.pin2
  N36: UM6522.pin24, 74LS05.4Y, 1K_ARRAY.pin2
  N37: UM6522.pin25, UM6522_2.pin25, 74LS05.5Y, 1K_ARRAY.pin3
  N38: UM6522_2.pin2, KC89C72_2.pin37
  N39: UM6522_2.pin3, KC89C72_2.pin36
  N40: UM6522_2.pin4, KC89C72_2.pin35
  N41: UM6522_2.pin5, KC89C72_2.pin34
  N42: UM6522_2.pin6, KC89C72_2.pin33
  N43: UM6522_2.pin7, KC89C72_2.pin32
  N44: UM6522_2.pin8, KC89C72_2.pin31
  N45: UM6522_2.pin9, KC89C72_2.pin30
  N46: UM6522_2.pin10, KC89C72_2.pin29
  N47: UM6522_2.pin11, KC89C72_2.pin27
  N48: UM6522_2.pin12, KC89C72_2.pin23
  N49: KC89C72_2.pin3, 330R_ARRAY_2.pin4
  N50: KC89C72_2.pin4, 330R_ARRAY_2.pin3
  N51: KC89C72_2.pin38, 330R_ARRAY_2.pin2
  N52: TRS1.Ring, 10uF_2.-, STEREO/MONO_SW.COM
  N53: TRS1.Tip, 10uF.-, STEREO/MONO_SW.L1, J6.pin2
  N54: 330R_ARRAY.pin1, 10uF.+, 330.Pin_1
  N55: 330R_ARRAY_2.pin1, 10uF_2.+, 330_2.Pin_1
  N56: 74LS05.2A, 74LS05.6Y, 4K7_ARRAY.pin2, 5pF.1
  N57: 74LS05.2Y, 74LS05.5A, 4K7_ARRAY.pin4, 5pF.0

notes:
  스피커

custom parts:
  Generic single row SMD female header - 25 pins: Generic single row SMD female header
  Solder Mask Keepout FC Cartridge Connector: 90-10.7
  Generic female header - 4 pins: Generic female header
