# Fritzing sketch OPLL-MIDISynth_byJCR (saved by Fritzing 1.0.3b)
circuit board: 8.46667cm x 5.64444cm
breadboards: 1

parts:
  Part1 = Arduino Nano (Rev3.0)
  TRS1 = Audio Jack (TRS) 3.5mm [package="4Ucon 08780 [THT]"]
  VBUS = Pad [width=3.861254072099717 height=3.430979727001059 connect=center]
  Power_plug1 = Power plug
  7805 = Voltage Regulator [package=78xxl]
  YM2413 = IC, DIP package, 18 pins [chip_label=IC]
  7805_2 = Voltage Regulator [package=78xxl]
  Part2 = Arduino Pro Mini v13
  74HC04 = 74HC04_HEX_INVERTER [package=dil14]
  PC817 = Sharp PC817 [package=THT]
  330 = Resistor [tolerance=±5% power=0.25W resistance=220 package=THT]
  1N4148 = Diode [package=diode-1n4148]
  1K = Resistor [tolerance=±5% power=0.25W resistance=220 package=THT]
  2_2K = Resistor [tolerance=±5% power=0.25W resistance=220 package=THT]
  2_2K_2 = Resistor [tolerance=±5% power=0.25W resistance=220 package=THT]
  UM3567 = IC, DIP package, 24 pins [chip_label=IC]
  LM4558N = IC, DIP package, 8 pins [chip_label=IC]
  2_2uF = Electrolytic Capacitor [capacitance=1µF voltage=35V package="100 mil [THT, electrolytic]"]
  4_7K = Resistor [tolerance=±5% power=0.25W resistance=220 package=THT]
  4_7K_2 = Resistor [tolerance=±5% power=0.25W resistance=220 package=THT]
  2_2uF_2 = Electrolytic Capacitor [capacitance=1µF voltage=35V package="100 mil [THT, electrolytic]"]
  1K_2 = Resistor [tolerance=±5% power=0.25W resistance=220 package=THT]
  82K = Resistor [tolerance=±5% power=0.25W resistance=220 package=THT]
  270pF = Ceramic Capacitor [capacitance=100nF voltage=35V package="100 mil [THT, multilayer]"]
  100K = Resistor [tolerance=±5% power=0.25W resistance=220 package=THT]
  100K_2 = Resistor [tolerance=±5% power=0.25W resistance=220 package=THT]
  33nF = Ceramic Capacitor [capacitance=100nF voltage=35V package="200 mil [THT, multilayer]"]
  10K = Resistor [tolerance=±5% power=0.25W resistance=220 package=THT]
  10K_2 = Resistor [tolerance=±5% power=0.25W resistance=220 package=THT]
  3_58MHz_Resonator = Resonator [frequency="16 Mhz" package=THT]

nets:
  N1: Part1.D0/RX, PC817.Pin_4, 1K.Pin_1
  GND: Part1.GND, Power_plug1.GND, 7805.GND, 7805_2.GND, 74HC04.GND, PC817.Pin_3
  VIN: Part1.VIN, Power_plug1.VCC, 7805.IN, 7805_2.IN
  N2: Part1.5V, 1K.Pin_0
  N3: TRS1.Sleeve, YM2413.pin1, 2_2K.Pin_1, 2_2K_2.Pin_1, UM3567.pin1, UM3567.pin9, UM3567.pin20, LM4558N.pin4, 100K.Pin_1, 33nF.1
  N4: TRS1.Ring, TRS1.Tip, 2_2uF.-
  N5: VBUS.pad, 7805.OUT, YM2413.pin16, 330.Pin_1, UM3567.pin21, LM4558N.pin8, 100K_2.Pin_0
  N6: YM2413.pin2, UM3567.pin2
  N7: YM2413.pin3, UM3567.pin3
  N8: YM2413.pin4, UM3567.pin4
  N9: YM2413.pin5, UM3567.pin6
  N10: YM2413.pin6, UM3567.pin7
  N11: YM2413.pin7, UM3567.pin8
  N12: YM2413.pin8, UM3567.pin10, 3_58MHz_Resonator.0
  N13: YM2413.pin9, UM3567.pin11, 3_58MHz_Resonator.pin_1
  N14: YM2413.pin10, UM3567.pin13
  N15: YM2413.pin11, UM3567.pin14
  N16: YM2413.pin12, UM3567.pin15
  N17: YM2413.pin13, UM3567.pin16
  N18: YM2413.pin14, 2_2K.Pin_0, 4_7K_2.Pin_0, 10K_2.Pin_1
  N19: YM2413.pin15, 2_2K_2.Pin_0, 4_7K.Pin_0, 10K.Pin_1
  N20: YM2413.pin17, UM3567.pin22
  N21: YM2413.pin18, UM3567.pin23
  N22: 7805_2.OUT, Part2.RAW, 74HC04.VCC
  GND_2: Part2.GND, 3_58MHz_Resonator.GND
  N23: Part2.D0/TX, 74HC04.1A
  N24: 74HC04.1Y, 74HC04.2A
  N25: 74HC04.2Y, PC817.Pin_2, 1N4148.A
  N26: PC817.Pin_1, 330.Pin_0, 1N4148.C
  N27: UM3567.pin18, 10K_2.Pin_0
  N28: UM3567.pin19, 10K.Pin_0
  N29: LM4558N.pin1, 2_2uF.+, 82K.Pin_1, 270pF.0
  N30: LM4558N.pin2, 1K_2.Pin_1
  N31: LM4558N.pin3, 82K.Pin_0, 270pF.1, 100K.Pin_0, 100K_2.Pin_1, 33nF.0
  N32: 4_7K.Pin_1, 4_7K_2.Pin_1, 2_2uF_2.+
  N33: 2_2uF_2.-, 1K_2.Pin_0

notes:
  USB
