# Fritzing sketch UM3567_to_YM2413 (saved by Fritzing 1.0.3b)
circuit board: 3.07682cm x 1.80478cm
breadboards: 1

parts:
  UM3567 = IC, DIP package, 24 pins [chip_label=IC]
  YM2413 = IC, DIP package, 18 pins [chip_label=IC]
  10K = Resistor [tolerance=±5% power=0.25W resistance=220 package=THT]
  10K1 = Resistor [tolerance=±5% power=0.25W resistance=220 package=THT]

nets:
  N1: UM3567.pin1, UM3567.pin9, UM3567.pin20, YM2413.pin1
  N2: UM3567.pin2, YM2413.pin2
  N3: UM3567.pin3, YM2413.pin3
  N4: UM3567.pin4, YM2413.pin4
  N5: UM3567.pin6, YM2413.pin5
  N6: UM3567.pin7, YM2413.pin6
  N7: UM3567.pin8, YM2413.pin7
  N8: UM3567.pin10, YM2413.pin8
  N9: UM3567.pin11, YM2413.pin9
  N10: UM3567.pin13, YM2413.pin10
  N11: UM3567.pin14, YM2413.pin11
  N12: UM3567.pin15, YM2413.pin12
  N13: UM3567.pin16, YM2413.pin13
  N14: UM3567.pin18, 10K1.Pin_0
  N15: UM3567.pin19, 10K.Pin_0
  N16: UM3567.pin21, YM2413.pin16
  N17: UM3567.pin22, YM2413.pin17
  N18: UM3567.pin23, YM2413.pin18
  N19: YM2413.pin14, 10K1.Pin_1
  N20: YM2413.pin15, 10K.Pin_1
