# Fritzing sketch YMZ284_AVR (saved by Fritzing 1.0.3b)
circuit board: 2.36233cm x 1.33717cm
breadboards: 1

parts:
  AVR = ATMEGA168 [package=mlf]
  IC1 = IC, DIP package, 16 pins [chip_label=IC]
  XTAL1 = Crystal [frequency="16 Mhz" package=THT]
  J1 = female pin header, 1 pin [form="♀ (female)"]
  2_2nF = Ceramic Capacitor [capacitance=100nF voltage=35V package="0805 [SMD, multilayer]"]
  5_8K = Resistor [tolerance=±5% resistance=220 power=0.25W package="0805 [SMD]"]
  5_8K_2 = Resistor [tolerance=±5% resistance=220 power=0.25W package="0805 [SMD]"]
  5_8K_3 = Resistor [tolerance=±5% resistance=220 power=0.25W package="0805 [SMD]"]

nets:
  N1: AVR.GND, IC1.pin6, J1.pin1
  N2: AVR.PB6(XTAL1_TOSC1), XTAL1.pin_1
  N3: AVR.PB7(XTAL2_TOSC2), XTAL1.pin_0
  N4: AVR.PB1(OC1A), 5_8K_2.Pin_1
  N5: AVR.PB2(SS_OC1B), 5_8K_3.Pin_1
  N6: AVR.PB3(MOSI_OC2), 5_8K.Pin_0
  N7: IC1.pin5, 2_2nF.0, 5_8K.Pin_1, 5_8K_2.Pin_0, 5_8K_3.Pin_0
