# Fritzing sketch Mapper183_ShuiGuanPipe (saved by Fritzing 1.0.3b)
circuit board: 9.00001cm x 5.68cm
breadboards: 1

parts:
  1-30 = Generic single row SMD female header - 30 pins [form="♀ (female)" package=THT]
  1_8K = Resistor [tolerance=±5% resistance=220 power=0.25W package=THT]
  100p = Ceramic Capacitor [capacitance=100nF voltage=35V package="200 mil [THT, multilayer]"]
  60-31 = Generic single row SMD female header - 30 pins [form="♀ (female)" package=THT]
  Pad1 = Pad [width=1.6352324469430506 height=2.70722996149219 connect=center]
  Pad2 = Pad [width=2.9318841568604044 height=1.5361188095537965 connect=center]
  IC1 = IC, DIP package, 32 pins [chip_label=IC]
  IC2 = IC, DIP package, 32 pins [chip_label=IC]
  AX5208C_/_VRC4 = IC, DIP package, 40 pins [chip_label=IC]
  74LS157 = IC, DIP package, 16 pins [chip_label=IC]
  74LS157_2 = IC, DIP package, 16 pins [chip_label=IC]
  74LS161 = IC, DIP package, 16 pins [chip_label=IC]
  1N4148 = Rectifier Diode [part_number=1N4001 package="300 mil [THT]"]
  Pad3 = Solder Mask Keepout FC Cartridge Connector  # not connected
  Pad4 = Solder Mask Keepout FC Cartridge Connector  # not connected
  VPP = Generic single row SMD female header - 2 pins [form="♀ (female)" package=THT]
  VPP_2 = Generic single row SMD female header - 2 pins [form="♀ (female)" package=THT]

nets:
  N1: 1-30.pin1, 1-30.pin16, 100p.0, Pad1.pad, IC1.pin16, IC1.pin24, IC2.pin16, IC2.pin24, AX5208C_/_VRC4.pin20, 74LS157.pin8, 74LS157.pin13, 74LS157.pin15, 74LS157_2.pin6, 74LS157_2.pin8, 74LS157_2.pin15, 74LS161.pin7, 74LS161.pin8, 74LS161.pin10
  N2: 1-30.pin2, IC1.pin25
  N3: 1-30.pin3, IC1.pin23
  N4: 1-30.pin4, IC1.pin26
  N5: 1-30.pin5, IC1.pin27
  N6: 1-30.pin6, IC1.pin5
  N7: 1-30.pin7, IC1.pin6
  N8: 1-30.pin8, IC1.pin7
  N9: 1-30.pin9, IC1.pin8
  N10: 1-30.pin10, IC1.pin9, AX5208C_/_VRC4.pin3
  N11: 1-30.pin11, IC1.pin10, AX5208C_/_VRC4.pin4, 74LS161.pin5
  N12: 1-30.pin12, IC1.pin11, 74LS161.pin4
  N13: 1-30.pin13, IC1.pin12, 74LS161.pin3
  N14: 1-30.pin14, AX5208C_/_VRC4.pin9, 74LS161.pin9
  N15: 1-30.pin15, AX5208C_/_VRC4.pin17
  N16: 1-30.pin17, AX5208C_/_VRC4.pin12
  N17: 1-30.pin18, AX5208C_/_VRC4.pin13
  N18: 1-30.pin19, IC2.pin6
  N19: 1-30.pin20, IC2.pin7
  N20: 1-30.pin21, IC2.pin8
  N21: 1-30.pin22, IC2.pin9
  N22: 1-30.pin23, IC2.pin10
  N23: 1-30.pin24, IC2.pin11
  N24: 1-30.pin25, IC2.pin12
  N25: 1-30.pin26, IC2.pin13
  N26: 1-30.pin27, IC2.pin14
  N27: 1-30.pin28, IC2.pin15
  N28: 1-30.pin29, IC2.pin17
  N29: 1-30.pin30, 60-31.pin1, Pad2.pad, IC1.pin31, IC1.pin32, IC2.pin31, IC2.pin32, AX5208C_/_VRC4.pin40, 74LS157.pin16, 74LS157_2.pin16, 74LS161.pin1, 74LS161.pin16, VPP.pin1, VPP_2.pin1
  N30: 1_8K.Pin_0, 100p.1, 74LS161.pin2, 1N4148.cathode
  N31: 1_8K.Pin_1, AX5208C_/_VRC4.pin19, 74LS157_2.pin10, 1N4148.anode
  N32: 60-31.pin2, AX5208C_/_VRC4.pin15
  N33: 60-31.pin3, IC1.pin4, 74LS157.pin14
  N34: 60-31.pin4, AX5208C_/_VRC4.pin1
  N35: 60-31.pin5, AX5208C_/_VRC4.pin2
  N36: 60-31.pin6, IC1.pin21
  N37: 60-31.pin7, IC1.pin20
  N38: 60-31.pin8, IC1.pin19
  N39: 60-31.pin9, IC1.pin18, AX5208C_/_VRC4.pin30
  N40: 60-31.pin10, IC1.pin17, AX5208C_/_VRC4.pin29
  N41: 60-31.pin11, IC1.pin15, AX5208C_/_VRC4.pin31
  N42: 60-31.pin12, IC1.pin14, AX5208C_/_VRC4.pin32
  N43: 60-31.pin13, IC1.pin13, AX5208C_/_VRC4.pin33
  N44: 60-31.pin14, AX5208C_/_VRC4.pin14, 74LS157.pin1, 74LS157_2.pin1
  N45: 60-31.pin15, 60-31.pin16
  N46: 60-31.pin18, 60-31.pin19
  N47: 60-31.pin20, IC2.pin5
  N48: 60-31.pin21, IC2.pin27
  N49: 60-31.pin22, IC2.pin26
  N50: 60-31.pin23, AX5208C_/_VRC4.pin7
  N51: 60-31.pin24, AX5208C_/_VRC4.pin6
  N52: 60-31.pin25, AX5208C_/_VRC4.pin5
  N53: 60-31.pin26, AX5208C_/_VRC4.pin11
  N54: 60-31.pin27, IC2.pin21
  N55: 60-31.pin28, IC2.pin20
  N56: 60-31.pin29, IC2.pin19
  N57: 60-31.pin30, IC2.pin18
  N58: IC1.pin1, VPP.pin2
  N59: IC1.pin2, 74LS157_2.pin4
  N60: IC1.pin3, 74LS157.pin9
  N61: IC1.pin22, 74LS157_2.pin9
  N62: IC1.pin28, 74LS157.pin4
  N63: IC1.pin29, 74LS157.pin7
  N64: IC1.pin30, 74LS157_2.pin7
  N65: IC2.pin1, VPP_2.pin2
  N66: IC2.pin2, AX5208C_/_VRC4.pin22
  N67: IC2.pin3, AX5208C_/_VRC4.pin27
  N68: IC2.pin4, AX5208C_/_VRC4.pin26
  N69: IC2.pin22, AX5208C_/_VRC4.pin10
  N70: IC2.pin23, AX5208C_/_VRC4.pin21
  N71: IC2.pin25, AX5208C_/_VRC4.pin23
  N72: IC2.pin28, AX5208C_/_VRC4.pin24
  N73: IC2.pin29, AX5208C_/_VRC4.pin25
  N74: AX5208C_/_VRC4.pin8, 74LS157_2.pin11
  N75: AX5208C_/_VRC4.pin34, 74LS157_2.pin2
  N76: AX5208C_/_VRC4.pin35, 74LS157.pin2
  N77: AX5208C_/_VRC4.pin36, 74LS157.pin5
  N78: AX5208C_/_VRC4.pin37, 74LS157.pin12
  N79: AX5208C_/_VRC4.pin38, 74LS157.pin11
  N80: AX5208C_/_VRC4.pin39, 74LS157_2.pin5
  N81: 74LS157.pin3, 74LS161.pin14
  N82: 74LS157.pin6, 74LS161.pin13
  N83: 74LS157.pin10, 74LS161.pin12
  N84: 74LS157_2.pin3, 74LS161.pin11

notes:
  水管PIPE Repro PCB. Designed by HeeminYT
  B L A C K   H O L E
  Gimmick!
  PRG-ROM
  CHR-ROM
  ◯
  lay this part down
  Honestly, those parts won't break even if this damn DIP40 chip lays an egg on top of them... Right?
  this board is freakin' crazy
  hi :3

custom parts:
  Generic single row SMD female header - 30 pins: Generic single row SMD female header
  Solder Mask Keepout FC Cartridge Connector: 90-10.7
  Generic single row SMD female header - 2 pins: Generic single row SMD female header
