# Fritzing sketch Mapper19_PacmanChampionshipEdition (saved by Fritzing 1.0.3b)
circuit board: 9.00001cm x 5.68cm
breadboards: 1

parts:
  1-30 = Generic single row SMD female header - 30 pins [form="♀ (female)" package=THT]
  60-31 = Generic single row SMD female header - 30 pins [form="♀ (female)" package=THT]
  27C1001 = IC, DIP package, 32 pins [chip_label=IC]
  27C1001_2 = IC, DIP package, 32 pins [chip_label=IC]  # not connected
  3564 = IC, DIP package, 28 pins [chip_label=IC]  # not connected
  N163 = Namco 129/163/175/340
  BAT1 = Battery Holders [package=battcom_20mm_pth]  # not connected

nets:
  N1: 1-30.pin2, 27C1001.pin25, N163.24
  N2: 1-30.pin3, 27C1001.pin23
  N3: 1-30.pin4, 27C1001.pin26
  N4: 1-30.pin5, 27C1001.pin27
  N5: 1-30.pin6, 27C1001.pin5
  N6: 1-30.pin7, 27C1001.pin6
  N7: 1-30.pin8, 27C1001.pin7
  N8: 1-30.pin9, 27C1001.pin8
  N9: 1-30.pin10, 27C1001.pin9
  N10: 1-30.pin11, 27C1001.pin10
  N11: 1-30.pin12, 27C1001.pin11
  N12: 1-30.pin13, 27C1001.pin12
  N13: 60-31.pin17, N163.28
  N14: 60-31.pin18, 27C1001.pin13, N163.21
  N15: 60-31.pin19, 27C1001.pin14, N163.20
  N16: 60-31.pin20, 27C1001.pin15, N163.18
  N17: 60-31.pin21, 27C1001.pin17, N163.17
  N18: 60-31.pin22, 27C1001.pin18, N163.16
  N19: 60-31.pin23, 27C1001.pin19, N163.15
  N20: 60-31.pin24, 27C1001.pin20, N163.14
  N21: 60-31.pin25, 27C1001.pin21, N163.13
  N22: 60-31.pin26, N163.27
  N23: 60-31.pin27, N163.26
  N24: 60-31.pin28, 27C1001.pin4, N163.25
  N25: 60-31.pin29, N163.30
  N26: 60-31.pin30, 27C1001.pin1
  N27: 27C1001.pin3, N163.10
  N28: 27C1001.pin22, N163.23
  N29: 27C1001.pin24, N163.9
  N30: 27C1001.pin28, N163.12
  N31: 27C1001.pin29, N163.11

custom parts:
  Generic single row SMD female header - 30 pins: Generic single row SMD female header
