# Fritzing sketch Mapper19_Pacmance_SRAM (saved by Fritzing 1.0.3b)
circuit board: 9.00001cm x 5.68cm
breadboards: 1

parts:
  1-30 = Generic single row SMD female header - 30 pins [form="♀ (female)" package=THT]
  60-31 = Generic single row SMD female header - 30 pins [form="♀ (female)" package=THT]
  Pad1 = Solder Mask Keepout FC Cartridge Connector  # not connected
  Pad2 = Solder Mask Keepout FC Cartridge Connector  # not connected
  Part1 = Namco 129/163/175/340
  4_7nF = Ceramic Capacitor [capacitance=100nF voltage=35V package="100 mil [THT, multilayer]"]
  10K = Resistor [tolerance=±5% power=0.25W resistance=220 package=THT]
  IC1 = IC, DIP package, 28 pins [chip_label=IC]
  IC2 = IC, DIP package, 28 pins [chip_label=IC]
  74HC1 = SO14 [chip_label=IC package=SO]
  FM16W8 = SO-28W [chip_label=IC package=SO(w)]
  74HC00 = SO14 [chip_label=IC package=SO]
  74HC00_2 = IC, DIP package, 14 pins [chip_label=IC]
  IC3 = IC, DIP package, 4 pins [chip_label=IC]
  IC4 = IC, DIP package, 4 pins [chip_label=IC]

nets:
  N1: 1-30.pin1, FM16W8.22
  N2: 1-30.pin2, Part1.24, IC1.pin23, FM16W8.23
  N3: 1-30.pin3, IC1.pin21, FM16W8.21
  N4: 1-30.pin4, IC1.pin24, FM16W8.24
  N5: 1-30.pin5, IC1.pin25, FM16W8.25
  N6: 1-30.pin6, IC1.pin3, FM16W8.3
  N7: 1-30.pin7, IC1.pin4, FM16W8.4
  N8: 1-30.pin8, IC1.pin5, FM16W8.5
  N9: 1-30.pin9, IC1.pin6, FM16W8.6
  N10: 1-30.pin10, IC1.pin7, FM16W8.7
  N11: 1-30.pin11, IC1.pin8, FM16W8.8
  N12: 1-30.pin12, IC1.pin9, FM16W8.9
  N13: 1-30.pin13, IC1.pin10, FM16W8.10
  N14: 1-30.pin14, Part1.29, FM16W8.27, 74HC00.5, IC3.pin3
  N15: 1-30.pin15, Part1.39
  N16: 1-30.pin16, Part1.6, Part1.31, 4_7nF.1, IC1.pin14, IC2.pin14, 74HC1.7, FM16W8.14, 74HC00.4, 74HC00.7, 74HC00_2.pin7
  N17: 1-30.pin17, Part1.33, IC2.pin22
  N18: 1-30.pin19, IC2.pin4
  N19: 1-30.pin20, IC2.pin5
  N20: 1-30.pin21, IC2.pin6
  N21: 1-30.pin22, IC2.pin7
  N22: 1-30.pin23, IC2.pin8
  N23: 1-30.pin24, IC2.pin9
  N24: 1-30.pin25, IC2.pin10
  N25: 1-30.pin26, IC2.pin11
  N26: 1-30.pin27, IC2.pin12
  N27: 1-30.pin28, IC2.pin13
  N28: 1-30.pin29, IC2.pin15
  N29: 1-30.pin30, 60-31.pin30, Part1.19, Part1.32, Part1.43, 74HC1.12, 74HC1.13, 74HC1.14, FM16W8.28, 74HC00.14, 74HC00_2.pin12, 74HC00_2.pin13, 74HC00_2.pin14, IC3.pin4, IC4.pin4
  N30: 60-31.pin1, IC2.pin16
  N31: 60-31.pin2, IC2.pin17
  N32: 60-31.pin3, IC2.pin18
  N33: 60-31.pin4, IC2.pin19
  N34: 60-31.pin5, Part1.35, 74HC1.1, 74HC00_2.pin1
  N35: 60-31.pin6, Part1.36, 74HC1.2, 74HC00_2.pin2
  N36: 60-31.pin7, Part1.37
  N37: 60-31.pin8, Part1.38
  N38: 60-31.pin9, IC2.pin24
  N39: 60-31.pin10, IC2.pin25
  N40: 60-31.pin11, IC2.pin3
  N41: 60-31.pin13, Part1.42, 74HC1.5, 74HC00_2.pin5
  N42: 60-31.pin14, IC4.pin3
  N43: 60-31.pin15, Part1.1, 4_7nF.0, 10K.Pin_0
  N44: 60-31.pin16, 10K.Pin_1
  N45: 60-31.pin17, Part1.28, IC1.pin20
  N46: 60-31.pin18, Part1.21, IC1.pin11, FM16W8.11
  N47: 60-31.pin19, Part1.20, IC1.pin12, FM16W8.12
  N48: 60-31.pin20, Part1.18, IC1.pin13, FM16W8.13
  N49: 60-31.pin21, Part1.17, IC1.pin15, FM16W8.15
  N50: 60-31.pin22, Part1.16, IC1.pin16, FM16W8.16
  N51: 60-31.pin23, Part1.15, IC1.pin17, FM16W8.17
  N52: 60-31.pin24, Part1.14, IC1.pin18, FM16W8.18
  N53: 60-31.pin25, Part1.13, IC1.pin19, FM16W8.19
  N54: 60-31.pin26, Part1.27
  N55: 60-31.pin27, Part1.26
  N56: 60-31.pin28, Part1.25, IC1.pin2, FM16W8.2
  N57: 60-31.pin29, Part1.30
  N58: Part1.2, IC2.pin26
  N59: Part1.3, IC2.pin2
  N60: Part1.4, IC2.pin23
  N61: Part1.5, IC2.pin21
  N62: Part1.8, IC1.pin28
  N63: Part1.9, IC3.pin2
  N64: Part1.10, IC1.pin1
  N65: Part1.11, IC1.pin27
  N66: Part1.12, IC1.pin26
  N67: Part1.23, IC1.pin22
  N68: Part1.40, 74HC00.1, 74HC00.2
  N69: Part1.45, IC2.pin28
  N70: Part1.46, IC4.pin2
  N71: Part1.47, IC2.pin1
  N72: Part1.48, IC2.pin27
  N73: IC2.pin20, 74HC1.6, 74HC00_2.pin6
  N74: 74HC1.3, 74HC1.4
  N75: 74HC1.9, 74HC1.10, 74HC1.11
  N76: FM16W8.20, 74HC00.8
  N77: 74HC00.3, 74HC00.10
  N78: 74HC00.6, 74HC00.9
  N79: 74HC00_2.pin3, 74HC00_2.pin4
  N80: 74HC00_2.pin9, 74HC00_2.pin10, 74HC00_2.pin11

notes:
  <-- 27C1001 --^

custom parts:
  Generic single row SMD female header - 30 pins: Generic single row SMD female header
  Solder Mask Keepout FC Cartridge Connector: 90-10.7
