# Fritzing sketch Mapper25_DynamiteBatmanVRC4 (saved by Fritzing 1.0.3b)
circuit board: 9.00001cm x 5.68cm
breadboards: 1

parts:
  1-30 = Generic single row SMD female header - 30 pins [form="♀ (female)" package=THT]
  60-31 = Generic single row SMD female header - 30 pins [form="♀ (female)" package=THT]
  Pad1 = Solder Mask Keepout FC Cartridge Connector  # not connected
  Pad2 = Solder Mask Keepout FC Cartridge Connector  # not connected
  VRC4 = IC, DIP package, 40 pins [chip_label=IC]
  27C1001 = IC, DIP package, 32 pins [chip_label=IC]
  6464_(Install_from_behind_the_board) = IC, DIP package, 28 pins [chip_label=IC]
  27C020 = IC, DIP package, 32 pins [chip_label=IC]

nets:
  N1: 1-30.pin10, VRC4.pin4
  N2: 1-30.pin11, VRC4.pin3
  N3: 1-30.pin14, VRC4.pin9
  N4: 1-30.pin15, VRC4.pin17
  N5: 1-30.pin17, VRC4.pin12
  N6: 1-30.pin18, VRC4.pin13
  N7: 60-31.pin5, VRC4.pin11
  N8: 60-31.pin6, VRC4.pin5
  N9: 60-31.pin7, VRC4.pin6
  N10: 60-31.pin8, VRC4.pin7
  N11: 60-31.pin17, VRC4.pin14
  N12: 60-31.pin26, VRC4.pin2
  N13: 60-31.pin27, VRC4.pin1
  N14: 60-31.pin29, VRC4.pin15
  N15: VRC4.pin8, 27C1001.pin22
  N16: VRC4.pin10, 27C020.pin22
  N17: VRC4.pin19, 6464_(Install_from_behind_the_board).pin20
  N18: VRC4.pin20, 27C020.pin16
  N19: VRC4.pin21, 27C020.pin23
  N20: VRC4.pin22, 27C020.pin2
  N21: VRC4.pin23, 27C020.pin25
  N22: 27C1001.pin4, 6464_(Install_from_behind_the_board).pin2
  N23: 27C1001.pin5, 6464_(Install_from_behind_the_board).pin3
  N24: 27C1001.pin6, 6464_(Install_from_behind_the_board).pin4
  N25: 27C1001.pin7, 6464_(Install_from_behind_the_board).pin5
  N26: 27C1001.pin8, 6464_(Install_from_behind_the_board).pin6
  N27: 27C1001.pin9, 6464_(Install_from_behind_the_board).pin7
  N28: 27C1001.pin10, 6464_(Install_from_behind_the_board).pin8
  N29: 27C1001.pin11, 6464_(Install_from_behind_the_board).pin9
  N30: 27C1001.pin12, 6464_(Install_from_behind_the_board).pin10
  N31: 27C1001.pin13, 6464_(Install_from_behind_the_board).pin11
  N32: 27C1001.pin14, 6464_(Install_from_behind_the_board).pin12
  N33: 27C1001.pin15, 6464_(Install_from_behind_the_board).pin13
  N34: 27C1001.pin16, 6464_(Install_from_behind_the_board).pin14
  N35: 27C1001.pin17, 6464_(Install_from_behind_the_board).pin15
  N36: 27C1001.pin18, 6464_(Install_from_behind_the_board).pin16
  N37: 27C1001.pin19, 6464_(Install_from_behind_the_board).pin17
  N38: 27C1001.pin20, 6464_(Install_from_behind_the_board).pin18
  N39: 27C1001.pin21, 6464_(Install_from_behind_the_board).pin19

custom parts:
  Generic single row SMD female header - 30 pins: Generic single row SMD female header
  Solder Mask Keepout FC Cartridge Connector: 90-10.7
