# Fritzing sketch Mapper85_DonkeyKongCountry4VRC7 (saved by Fritzing 1.0.3b)
circuit board: 9.00001cm x 5.68cm
breadboards: 1

parts:
  1-30 = Generic single row SMD female header - 30 pins [form="♀ (female)" package=THT]
  60-31 = Generic single row SMD female header - 30 pins [form="♀ (female)" package=THT]
  3_58MHz = Crystal [frequency="16 Mhz" package=SMD]
  3_9K = Resistor [tolerance=±5% power=0.25W resistance=220 package=THT]
  2_2K = Resistor [tolerance=±5% power=0.25W resistance=220 package=THT]
  27C040 = IC, DIP package, 32 pins [chip_label=IC]
  VRC_VII_053982 = IC, DIP package, 48 pins [chip_label=IC]
  Pad1 = Pad [width=1.8450698756469115 height=2.0987357935497952 connect=center]
  Pad2 = Pad [width=1.8450698756469115 height=2.0987357935497952 connect=center]
  Pad3 = Pad [width=1.8450698756469115 height=2.0987357935497952 connect=center]
  18pf = Ceramic Capacitor [capacitance=100nF voltage=35V package="1206 [SMD, multilayer]"]
  18pf1 = Ceramic Capacitor [capacitance=100nF voltage=35V package="1206 [SMD, multilayer]"]
  27C020 = IC, DIP package, 32 pins [chip_label=IC]
  VPP = Generic single row SMD female header - 2 pins [form="♀ (female)" package=THT]
  VPP_2 = Generic single row SMD female header - 2 pins [form="♀ (female)" package=THT]
  Pad4 = Solder Mask Keepout FC Cartridge Connector  # not connected
  Pad5 = Solder Mask Keepout FC Cartridge Connector  # not connected
  1uF = Ceramic Capacitor [capacitance=100nF voltage=35V package="100 mil [THT, multilayer]"]
  240K = Resistor [tolerance=±5% power=0.25W resistance=220 package=THT]
  910 = Resistor [tolerance=±5% power=0.25W resistance=220 package=THT]
  4_3K = Resistor [tolerance=±5% power=0.25W resistance=220 package=THT]
  22uF = Ceramic Capacitor [capacitance=100nF voltage=35V package="100 mil [THT, multilayer]"]
  33K = Resistor [tolerance=±5% power=0.25W resistance=220 package=THT]
  4_7nF = Ceramic Capacitor [capacitance=100nF voltage=35V package="100 mil [THT, multilayer]"]
  2_2K_2 = Resistor [tolerance=±5% power=0.25W resistance=220 package=THT]
  27K = Resistor [tolerance=±5% power=0.25W resistance=220 package=THT]
  LM359 = LM 358 Dual Op-Amp [package="SO 08 [SMD]"]
  2OP_AMP = LM 358 Dual Op-Amp [package="DIP8 [THT]"]
  39SF040 = Generic single row SMD female header - 2 pins [form="♀ (female)" package=THT]
  27C040_2 = Generic single row SMD female header - 2 pins [form="♀ (female)" package=THT]
  Pad6 = Pad [width=1.791881653391696 height=1.3177983052141493 connect=center]

nets:
  N1: 1-30.pin1, 27C040.pin16, 27C040.pin24, VRC_VII_053982.pin24, Pad2.pad, 18pf.1, 18pf1.0
  N2: 1-30.pin2, 27C040.pin25
  N3: 1-30.pin3, 27C040.pin23
  N4: 1-30.pin4, 27C040.pin26
  N5: 1-30.pin5, 27C040.pin27
  N6: 1-30.pin6, 27C040.pin5
  N7: 1-30.pin7, 27C040.pin6
  N8: 1-30.pin8, 27C040.pin7, VRC_VII_053982.pin16
  N9: 1-30.pin9, 27C040.pin8, VRC_VII_053982.pin19
  N10: 1-30.pin10, 27C040.pin9
  N11: 1-30.pin11, 27C040.pin10
  N12: 1-30.pin12, 27C040.pin11
  N13: 1-30.pin13, 27C040.pin12
  N14: 1-30.pin14, VRC_VII_053982.pin4
  N15: 1-30.pin15, VRC_VII_053982.pin5
  N16: 1-30.pin16, VRC_VII_053982.pin3, VRC_VII_053982.pin46, 27C020.pin16, 27C020.pin22, 27C020.pin24, 1uF.0, 910.Pin_1, 22uF.1, 33K.Pin_0, 4_7nF.1, 2_2K_2.Pin_0, LM359.connector3, 2OP_AMP.connector3
  N17: 1-30.pin17, VRC_VII_053982.pin1
  N18: 1-30.pin18, VRC_VII_053982.pin6
  N19: 1-30.pin19, 27C020.pin6
  N20: 1-30.pin20, 27C020.pin7
  N21: 1-30.pin21, 27C020.pin8
  N22: 1-30.pin22, 27C020.pin9
  N23: 1-30.pin23, 27C020.pin10
  N24: 1-30.pin24, 27C020.pin11
  N25: 1-30.pin25, 27C020.pin12
  N26: 1-30.pin26, 27C020.pin13
  N27: 1-30.pin27, 27C020.pin14
  N28: 1-30.pin28, 27C020.pin15
  N29: 1-30.pin29, 27C020.pin17
  N30: 1-30.pin30, 60-31.pin30, 27C040.pin32, VRC_VII_053982.pin15, VRC_VII_053982.pin30, VRC_VII_053982.pin42, 27C020.pin31, 27C020.pin32, VPP.pin1, VPP_2.pin2, 1uF.1, LM359.connector4, LM359.connector5, LM359.connector7, 2OP_AMP.connector4, 2OP_AMP.connector5, 2OP_AMP.connector7, Pad6.pad
  N31: 60-31.pin1, 27C020.pin18
  N32: 60-31.pin2, 27C020.pin19
  N33: 60-31.pin3, 27C020.pin20
  N34: 60-31.pin4, 27C020.pin21
  N35: 60-31.pin5, VRC_VII_053982.pin2
  N36: 60-31.pin6, VRC_VII_053982.pin33
  N37: 60-31.pin7, VRC_VII_053982.pin32
  N38: 60-31.pin8, VRC_VII_053982.pin31
  N39: 60-31.pin9, 27C020.pin26
  N40: 60-31.pin10, 27C020.pin27
  N41: 60-31.pin11, 27C020.pin5
  N42: 60-31.pin12, 60-31.pin13
  N43: 60-31.pin15, 3_9K.Pin_0, 2_2K.Pin_1
  N44: 60-31.pin16, 3_9K.Pin_1
  N45: 60-31.pin17, VRC_VII_053982.pin45
  N46: 60-31.pin18, 27C040.pin13, VRC_VII_053982.pin7
  N47: 60-31.pin19, 27C040.pin14, VRC_VII_053982.pin8
  N48: 60-31.pin20, 27C040.pin15, VRC_VII_053982.pin9
  N49: 60-31.pin21, 27C040.pin17, VRC_VII_053982.pin10
  N50: 60-31.pin22, 27C040.pin18, VRC_VII_053982.pin11
  N51: 60-31.pin23, 27C040.pin19, VRC_VII_053982.pin12
  N52: 60-31.pin24, 27C040.pin20, VRC_VII_053982.pin13
  N53: 60-31.pin25, 27C040.pin21, VRC_VII_053982.pin14
  N54: 60-31.pin26, VRC_VII_053982.pin29
  N55: 60-31.pin27, VRC_VII_053982.pin28
  N56: 60-31.pin28, 27C040.pin4, VRC_VII_053982.pin27
  N57: 60-31.pin29, VRC_VII_053982.pin47
  N58: 3_58MHz.pin_0, VRC_VII_053982.pin18, Pad3.pad, 18pf1.1
  N59: 3_58MHz.pin_1, VRC_VII_053982.pin17, Pad1.pad, 18pf.0
  N60: 2_2K.Pin_0, 240K.Pin_1, 910.Pin_0, LM359.connector0, 2OP_AMP.connector0
  N61: 27C040.pin1, VPP.pin2, 39SF040.pin1
  N62: 27C040.pin2, VRC_VII_053982.pin23
  N63: 27C040.pin3, VRC_VII_053982.pin22
  N64: 27C040.pin22, VRC_VII_053982.pin44
  N65: 27C040.pin28, VRC_VII_053982.pin20
  N66: 27C040.pin29, VRC_VII_053982.pin21
  N67: 27C040.pin30, VRC_VII_053982.pin25
  N68: 27C040.pin31, 27C040_2.pin2
  N69: VRC_VII_053982.pin26, 39SF040.pin2, 27C040_2.pin1
  N70: VRC_VII_053982.pin34, 27C020.pin23
  N71: VRC_VII_053982.pin35, 27C020.pin25
  N72: VRC_VII_053982.pin36, 27C020.pin4
  N73: VRC_VII_053982.pin37, 27C020.pin28
  N74: VRC_VII_053982.pin38, 27C020.pin29
  N75: VRC_VII_053982.pin39, 27C020.pin3
  N76: VRC_VII_053982.pin40, 27C020.pin2
  N77: VRC_VII_053982.pin41, 27C020.pin30
  N78: VRC_VII_053982.pin43, 2_2K_2.Pin_1, 27K.Pin_1
  N79: 27C020.pin1, VPP_2.pin1
  N80: 240K.Pin_0, 4_3K.Pin_0, LM359.connector1, 2OP_AMP.connector1
  N81: 4_3K.Pin_1, 22uF.0
  N82: 33K.Pin_1, 4_7nF.0, 27K.Pin_0, LM359.connector2, 2OP_AMP.connector2
  N83: LM359.connector6, 2OP_AMP.connector6

notes:
  DKC4 VRC7 Designed by HeeminYT

custom parts:
  Generic single row SMD female header - 30 pins: Generic single row SMD female header
  Generic single row SMD female header - 2 pins: Generic single row SMD female header
  Solder Mask Keepout FC Cartridge Connector: 90-10.7
