# Fritzing sketch MapperUNDEFINED_LuigiMansion (saved by Fritzing 1.0.3b)
circuit board: 9.00001cm x 8.67999cm
breadboards: 1

parts:
  1-30 = Generic single row SMD female header - 30 pins [form="♀ (female)" package=THT]
  60-31 = Generic single row SMD female header - 30 pins [form="♀ (female)" package=THT]
  Pad1 = Solder Mask Keepout FC Cartridge Connector  # not connected
  Pad2 = Solder Mask Keepout FC Cartridge Connector  # not connected
  IC2 = IC, DIP package, 40 pins [chip_label=IC]
  IC3 = IC, DIP package, 48 pins [chip_label=IC]
  IC6 = IC, DIP package, 32 pins [chip_label=IC]
  IC7 = IC, DIP package, 28 pins [chip_label=IC]
  IC4 = IC, DIP package, 42 pins [chip_label=IC]
  0Ω = Resistor [tolerance=±5% power=0.25W resistance=220 package=THT]
  3KΩ = Resistor [tolerance=±5% power=0.25W resistance=220 package=THT]
  3KΩ_2 = Resistor [tolerance=±5% power=0.25W resistance=220 package=THT]
  240 = Resistor [tolerance=±5% power=0.25W resistance=220 package=THT]
  1uF = Ceramic Capacitor [capacitance=100nF voltage=35V package="100 mil [THT, multilayer]"]
  J2B = female pin header, 1 pin [form="♀ (female)"]
  3KΩ_3 = Resistor [tolerance=±5% power=0.25W resistance=220 package=THT]
  J1 = female pin header, 2 pins [form="♀ (female)"]  # not connected
  IC9 = IC, DIP package, 16 pins [chip_label=IC]
  BAT1 = Battery Holders [package=battcom_20mm_pth]
  10K = Resistor [tolerance=±5% power=0.25W resistance=220 package=THT]
  1KΩ = Resistor [tolerance=±5% power=0.25W resistance=220 package=THT]
  EBC = TRANSISTOR_NPN [package=to-92]
  IC8 = IC, DIP package, 14 pins [chip_label=IC]
  J3 = Generic single row SMD female header - 2 pins [form="♀ (female)" package=THT]
  D1 = Rectifier Diode [part_number=1N4001 package="300 mil [THT]"]
  0_1uF = Ceramic Capacitor [capacitance=100nF voltage=35V package="100 mil [THT, multilayer]"]
  3KΩ_4 = Resistor [tolerance=±5% power=0.25W resistance=220 package=THT]
  330 = Resistor [tolerance=±5% power=0.25W resistance=220 package=THT]
  0_1uF_2 = Ceramic Capacitor [capacitance=100nF voltage=35V package="100 mil [THT, multilayer]"]
  1KΩ_2 = Resistor [tolerance=±5% power=0.25W resistance=220 package=THT]
  1KΩ_3 = Resistor [tolerance=±5% power=0.25W resistance=220 package=THT]
  J1B = female pin header, 1 pin [form="♀ (female)"]
  J1A = female pin header, 1 pin [form="♀ (female)"]
  J2A = female pin header, 1 pin [form="♀ (female)"]

nets:
  N1: 1-30.pin1, 1-30.pin16, IC2.pin1, IC2.pin24, IC2.pin29, IC3.pin18, IC6.pin16, IC6.pin22, IC7.pin6, IC7.pin20, IC4.pin12, IC4.pin31, IC4.pin32, 1uF.1, IC9.pin1, IC9.pin8, BAT1.-, EBC.E, IC8.pin7, 3KΩ_4.Pin_0, 0_1uF_2.0
  N2: 1-30.pin2, IC3.pin41, IC6.pin25
  N3: 1-30.pin3, IC3.pin39, IC6.pin23
  N4: 1-30.pin4, IC3.pin42, IC6.pin26
  N5: 1-30.pin5, IC3.pin43, IC6.pin27
  N6: 1-30.pin6, IC6.pin5
  N7: 1-30.pin7, IC3.pin6, IC6.pin6
  N8: 1-30.pin8, IC3.pin7, IC6.pin7
  N9: 1-30.pin9, IC3.pin8, IC6.pin8
  N10: 1-30.pin10, IC3.pin9, IC6.pin9
  N11: 1-30.pin11, IC3.pin10, IC6.pin10
  N12: 1-30.pin12, IC3.pin11, IC6.pin11
  N13: 1-30.pin13, IC3.pin12, IC6.pin12
  N14: 1-30.pin14, IC3.pin16, IC9.pin13
  N15: 1-30.pin17, IC4.pin13
  N16: 1-30.pin18, IC3.pin31
  N17: 1-30.pin19, IC4.pin5
  N18: 1-30.pin20, IC4.pin6
  N19: 1-30.pin21, IC4.pin7
  N20: 1-30.pin22, IC4.pin8
  N21: 1-30.pin23, IC4.pin9
  N22: 1-30.pin24, IC4.pin10
  N23: 1-30.pin25, IC4.pin30
  N24: 1-30.pin26, IC4.pin14
  N25: 1-30.pin27, IC4.pin16
  N26: 1-30.pin28, IC4.pin18
  N27: 1-30.pin29, IC4.pin20
  N28: 1-30.pin30, 60-31.pin30, IC2.pin25, IC2.pin40, IC3.pin48, IC6.pin32, IC7.pin3, IC7.pin17, IC4.pin22, IC9.pin16, 1KΩ.Pin_1, IC8.pin14
  N29: 60-31.pin1, IC4.pin23
  N30: 60-31.pin2, IC4.pin25
  N31: 60-31.pin3, IC4.pin27
  N32: 60-31.pin4, IC4.pin29
  N33: 60-31.pin5, IC4.pin11
  N34: 60-31.pin6, IC3.pin23
  N35: 60-31.pin7, IC3.pin22
  N36: 60-31.pin8, IC3.pin21
  N37: 60-31.pin9, IC4.pin41
  N38: 60-31.pin10, IC4.pin3
  N39: 60-31.pin11, IC4.pin4
  N40: 60-31.pin12, 60-31.pin13
  N41: 60-31.pin15, J1A.pin1
  N42: 60-31.pin16, J2A.pin1
  N43: 60-31.pin17, IC3.pin38, IC6.pin24, IC9.pin15
  N44: 60-31.pin18, IC2.pin37, IC3.pin13, IC6.pin13, IC7.pin28
  N45: 60-31.pin19, IC2.pin36, IC3.pin14, IC6.pin14, IC7.pin27
  N46: 60-31.pin20, IC2.pin35, IC3.pin15, IC6.pin15, IC7.pin26
  N47: 60-31.pin21, IC3.pin33, IC6.pin17
  N48: 60-31.pin22, IC2.pin33, IC3.pin34, IC6.pin18, IC7.pin24
  N49: 60-31.pin23, IC2.pin32, IC3.pin35, IC6.pin19, IC7.pin23
  N50: 60-31.pin24, IC2.pin31, IC3.pin36, IC6.pin20, IC7.pin22
  N51: 60-31.pin25, IC2.pin30, IC3.pin37, IC6.pin21, IC7.pin21
  N52: 60-31.pin26, IC3.pin5, IC9.pin14
  N53: 60-31.pin27, IC2.pin28, IC3.pin4, IC7.pin19
  N54: 60-31.pin28, IC3.pin3, IC6.pin4
  N55: 60-31.pin29, IC3.pin2, 0Ω.Pin_0, J3.pin1
  N56: IC2.pin3, IC7.pin4, 3KΩ.Pin_0
  N57: IC2.pin4, IC7.pin5, 3KΩ_2.Pin_0
  N58: IC2.pin14, IC7.pin7
  N59: IC2.pin15, IC7.pin8
  N60: IC2.pin16, IC7.pin9
  N61: IC2.pin17, IC7.pin10
  N62: IC2.pin18, IC7.pin11, IC4.pin42
  N63: IC2.pin19, IC7.pin12, IC4.pin1
  N64: IC2.pin20, IC7.pin13, IC4.pin2
  N65: IC2.pin21, IC7.pin14, 10K.Pin_0, IC8.pin6, IC8.pin12
  N66: IC2.pin22, IC7.pin15
  N67: IC2.pin23, IC7.pin16, 0Ω.Pin_1, J3.pin2
  N68: IC2.pin27, IC7.pin18, IC9.pin7
  N69: IC2.pin34, IC3.pin32, IC7.pin25
  N70: IC2.pin38, IC7.pin1
  N71: IC2.pin39, 3KΩ_3.Pin_0
  N72: IC3.pin1, IC6.pin1
  N73: IC3.pin17, IC4.pin33
  N74: IC3.pin19, IC4.pin35
  N75: IC3.pin20, IC4.pin38
  N76: IC3.pin24, BAT1.+, D1.anode
  N77: IC3.pin25, D1.cathode
  N78: IC3.pin26, IC4.pin40
  N79: IC3.pin27, IC4.pin34
  N80: IC3.pin28, IC4.pin39
  N81: IC3.pin29, IC4.pin37
  N82: IC3.pin30, IC4.pin36
  N83: IC3.pin40, IC6.pin2
  N84: IC3.pin44, IC6.pin28
  N85: IC3.pin45, IC6.pin29
  N86: IC3.pin46, IC6.pin3
  N87: IC3.pin47, IC6.pin30
  N88: 3KΩ.Pin_1, 3KΩ_2.Pin_1, IC8.pin1, IC8.pin3
  N89: 240.Pin_0, 1uF.0, IC8.pin4, 330.Pin_0, 0_1uF_2.1, 1KΩ_2.Pin_1
  N90: 240.Pin_1, IC8.pin10
  N91: J2B.pin1, 1KΩ_2.Pin_0, 1KΩ_3.Pin_1
  N92: 3KΩ_3.Pin_1, IC8.pin9, IC8.pin11
  N93: IC9.pin2, IC9.pin3, IC9.pin11
  N94: 10K.Pin_1, EBC.B
  N95: 1KΩ.Pin_0, EBC.C, IC8.pin5, IC8.pin13
  N96: IC8.pin2, IC8.pin8, 0_1uF.1
  N97: 0_1uF.0, 3KΩ_4.Pin_1, 330.Pin_1
  N98: 1KΩ_3.Pin_0, J1B.pin1

notes:
  HM-89X72

custom parts:
  Generic single row SMD female header - 30 pins: Generic single row SMD female header
  Solder Mask Keepout FC Cartridge Connector: 90-10.7
  Generic single row SMD female header - 2 pins: Generic single row SMD female header
