# Fritzing sketch MapperUNKNOWN_20in1 (saved by Fritzing 1.0.3b)
circuit board: 9.00001cm x 5.68cm
breadboards: 1

parts:
  1-30 = Generic single row SMD female header - 30 pins [form="♀ (female)" package=THT]
  60-31 = Generic single row SMD female header - 30 pins [form="♀ (female)" package=THT]  # not connected
  Pad1 = Solder Mask Keepout FC Cartridge Connector  # not connected
  Pad2 = Solder Mask Keepout FC Cartridge Connector  # not connected
  27C040-PRG2 = IC, DIP package, 32 pins [chip_label=IC]
  xx64 = IC, DIP package, 28 pins [chip_label=IC]
  74HC139N = 74HC139N [part_number=74HC139N package="DIP (Dual Inline) [THT]"]  # not connected
  74LS273 = IC, DIP package, 20 pins [chip_label=IC]  # not connected
  74LS153 = IC, DIP package, 16 pins [chip_label=IC]  # not connected
  74LS02 = IC, DIP package, 14 pins [chip_label=IC]
  27C040-PRG1 = IC, DIP package, 32 pins [chip_label=IC]
  2N2222 = NPN-Transistor [package="TO92 [THT]"]
  10K = Resistor [tolerance=±5% power=0.25W resistance=220 package=THT]
  1K = Resistor [tolerance=±5% power=0.25W resistance=220 package=THT]

nets:
  N1: 1-30.pin16, 27C040-PRG2.pin16
  N2: 1-30.pin19, xx64.pin4
  N3: 1-30.pin20, xx64.pin5
  N4: 1-30.pin21, xx64.pin6
  N5: 1-30.pin22, xx64.pin7
  N6: 1-30.pin23, xx64.pin8
  N7: 1-30.pin24, xx64.pin9
  N8: 1-30.pin25, xx64.pin10
  N9: 1-30.pin26, xx64.pin11
  N10: 1-30.pin27, xx64.pin12
  N11: 1-30.pin28, xx64.pin13
  N12: 27C040-PRG2.pin24, 2N2222.E, 1K.Pin_0
  N13: 74LS02.pin13, 27C040-PRG1.pin24, 10K.Pin_1
  N14: 2N2222.B, 10K.Pin_0

custom parts:
  Generic single row SMD female header - 30 pins: Generic single row SMD female header
  Solder Mask Keepout FC Cartridge Connector: 90-10.7
