# Fritzing sketch ShuiGuanPipe (saved by Fritzing 1.0.3b)
circuit board: 9.00001cm x 5.68cm
breadboards: 1

parts:
  1-30 = Generic single row SMD female header - 30 pins [form="♀ (female)" package=THT]
  1_8K = Resistor [tolerance=±5% resistance=220 power=0.25W package=THT]
  74LS161 = IC, DIP package, 16 pins [chip_label=IC]
  74LS157 = IC, DIP package, 16 pins [chip_label=IC]
  AX5208C_/_VRC4 = IC, DIP package, 40 pins [chip_label=IC]
  100p = Ceramic Capacitor [capacitance=100nF voltage=35V package="200 mil [THT, multilayer]"]
  60-31 = Generic single row SMD female header - 30 pins [form="♀ (female)" package=THT]
  IC1 = IC, DIP package, 32 pins [chip_label=IC]
  IC2 = IC, DIP package, 32 pins [chip_label=IC]
  Pad1 = Pad [width=1.6352324469430506 height=2.70722996149219 connect=center]
  74LS157_2 = IC, DIP package, 16 pins [chip_label=IC]
  27C1 = 27C020 EEPROM [chip_label=27C020 package="DIP (Dual Inline) [THT]"]  # not connected
  Pad2 = Pad [width=2.9318841568604044 height=1.5361188095537965 connect=center]
  D1 = Rectifier Diode [part_number=1N4001 package="300 mil [THT]"]
  JUMPER1-A = Pad [width=1.303826638430197 height=1.5168892194457975 connect=center]
  JUMPER2-A = Pad [width=2 height=1.2 connect=center]
  JUMPER2-B = Pad [width=2 height=1.2 connect=center]  # not connected
  JUMPER1-B = Pad [width=1.303826638430197 height=1.5168892194457975 connect=center]

nets:
  N1: 1-30.pin1, 74LS161.pin7, 74LS161.pin10, 74LS157.pin6, 74LS157.pin15, AX5208C_/_VRC4.pin20, 100p.0, IC1.pin24, IC2.pin24, Pad1.pad, 74LS157_2.pin13, 74LS157_2.pin15
  N2: 1-30.pin2, IC1.pin25
  N3: 1-30.pin3, IC1.pin23
  N4: 1-30.pin4, IC1.pin26
  N5: 1-30.pin5, IC1.pin27
  N6: 1-30.pin6, IC1.pin5
  N7: 1-30.pin7, IC1.pin6
  N8: 1-30.pin8, IC1.pin7
  N9: 1-30.pin9, IC1.pin8
  N10: 1-30.pin10, AX5208C_/_VRC4.pin3, IC1.pin9
  N11: 1-30.pin11, 74LS161.pin5, AX5208C_/_VRC4.pin4, IC1.pin10
  N12: 1-30.pin12, 74LS161.pin4, IC1.pin11
  N13: 1-30.pin13, 74LS161.pin3, IC1.pin12
  N14: 1-30.pin14, 74LS161.pin9, AX5208C_/_VRC4.pin9
  N15: 1-30.pin15, AX5208C_/_VRC4.pin17
  N16: 1-30.pin16, IC1.pin16, IC2.pin16
  N17: 1-30.pin17, AX5208C_/_VRC4.pin12
  N18: 1-30.pin18, AX5208C_/_VRC4.pin13
  N19: 1-30.pin19, IC2.pin6
  N20: 1-30.pin20, IC2.pin7
  N21: 1-30.pin21, IC2.pin8
  N22: 1-30.pin22, IC2.pin9
  N23: 1-30.pin23, IC2.pin10
  N24: 1-30.pin24, IC2.pin11
  N25: 1-30.pin25, IC2.pin12
  N26: 1-30.pin26, IC2.pin13
  N27: 1-30.pin27, IC2.pin14
  N28: 1-30.pin28, IC2.pin15
  N29: 1-30.pin29, IC2.pin17
  N30: 1-30.pin30, IC2.pin32
  N31: 1_8K.Pin_0, 74LS161.pin2, 100p.1, D1.cathode
  N32: 1_8K.Pin_1, 74LS157.pin10, AX5208C_/_VRC4.pin19, D1.anode
  N33: 74LS161.pin1, 74LS157.pin16, AX5208C_/_VRC4.pin40, 60-31.pin1, IC1.pin31, IC1.pin32, 74LS157_2.pin16, Pad2.pad
  N34: 74LS161.pin11, 74LS157.pin3
  N35: 74LS161.pin12, 74LS157_2.pin10
  N36: 74LS161.pin13, 74LS157_2.pin6
  N37: 74LS161.pin14, 74LS157_2.pin3
  N38: 74LS157.pin1, AX5208C_/_VRC4.pin14, 60-31.pin14, 74LS157_2.pin1
  N39: 74LS157.pin2, AX5208C_/_VRC4.pin34
  N40: 74LS157.pin4, IC1.pin2
  N41: 74LS157.pin5, AX5208C_/_VRC4.pin39
  N42: 74LS157.pin7, IC1.pin30
  N43: 74LS157.pin9, IC1.pin22
  N44: 74LS157.pin11, AX5208C_/_VRC4.pin8
  N45: AX5208C_/_VRC4.pin1, 60-31.pin4, JUMPER2-A.pad
  N46: AX5208C_/_VRC4.pin2, JUMPER1-A.pad
  N47: AX5208C_/_VRC4.pin5, 60-31.pin25
  N48: AX5208C_/_VRC4.pin6, 60-31.pin24
  N49: AX5208C_/_VRC4.pin7, 60-31.pin23
  N50: AX5208C_/_VRC4.pin10, IC2.pin22
  N51: AX5208C_/_VRC4.pin11, 60-31.pin26
  N52: AX5208C_/_VRC4.pin21, IC2.pin23
  N53: AX5208C_/_VRC4.pin22, IC2.pin2
  N54: AX5208C_/_VRC4.pin23, IC2.pin25
  N55: AX5208C_/_VRC4.pin24, IC2.pin28
  N56: AX5208C_/_VRC4.pin25, IC2.pin29
  N57: AX5208C_/_VRC4.pin26, IC2.pin4
  N58: AX5208C_/_VRC4.pin27, IC2.pin3
  N59: AX5208C_/_VRC4.pin29, 60-31.pin10, IC1.pin17
  N60: AX5208C_/_VRC4.pin30, 60-31.pin9, IC1.pin18
  N61: AX5208C_/_VRC4.pin31, 60-31.pin11, IC1.pin15
  N62: AX5208C_/_VRC4.pin32, 60-31.pin12, IC1.pin14
  N63: AX5208C_/_VRC4.pin33, 60-31.pin13, IC1.pin13
  N64: AX5208C_/_VRC4.pin35, 74LS157_2.pin2
  N65: AX5208C_/_VRC4.pin36, 74LS157_2.pin5
  N66: AX5208C_/_VRC4.pin37, 74LS157_2.pin12
  N67: AX5208C_/_VRC4.pin38, 74LS157_2.pin11
  N68: 60-31.pin3, IC1.pin4, 74LS157_2.pin14
  N69: 60-31.pin5, JUMPER1-B.pad
  N70: 60-31.pin6, IC1.pin21
  N71: 60-31.pin7, IC1.pin20
  N72: 60-31.pin8, IC1.pin19
  N73: 60-31.pin20, IC2.pin5
  N74: 60-31.pin21, IC2.pin27
  N75: 60-31.pin22, IC2.pin26
  N76: 60-31.pin27, IC2.pin21
  N77: 60-31.pin28, IC2.pin20
  N78: 60-31.pin29, IC2.pin19
  N79: 60-31.pin30, IC2.pin18
  N80: IC1.pin3, 74LS157_2.pin9
  N81: IC1.pin28, 74LS157_2.pin4
  N82: IC1.pin29, 74LS157_2.pin7

notes:
  水管PIPE Repro PCB. Designed by HeeminYT
  wtf??
  __________________
  ________________________
  Gimmick!

custom parts:
  Generic single row SMD female header - 30 pins: Generic single row SMD female header
  27C020 EEPROM: An EPROM (rarely EROM), or erasable programmable read-only memory, is a type of programmable read-only memory (PROM) chip that retains its data when its power supply is switched off.
